// Logisim project videoadapterebat.circ as structural Verilog: 6 circuits, main circuit main
module main (
  input  reset,
  input  change_value,
  input  [3:0] column,
  input  _0_if_start_pos_else_1,
  input  [3:0] row,
  output [15:0] out_6,
  output [15:0] out_7,
  output [15:0] out_8,
  output [15:0] out_9,
  output [15:0] out_10,
  output [15:0] out_11,
  output [15:0] out_12,
  output [15:0] out_13,
  output [15:0] out_14,
  output [15:0] out_15,
  output [15:0] out_16,
  output [15:0] out_17,
  output [15:0] out_18,
  output [15:0] out_19,
  output [15:0] out_20,
  output [15:0] out_21
);

  wire decoder_1_out0, decoder_1_out1, decoder_1_out2, decoder_1_out3, decoder_1_out4, decoder_1_out5,
       decoder_1_out6, decoder_1_out7, decoder_1_out8, decoder_1_out9, decoder_1_out10, decoder_1_out11,
       decoder_1_out12, decoder_1_out13, decoder_1_out14, decoder_1_out15, or_1_out;

  Decoder #(.select(4)) decoder_1 (
    .out0(decoder_1_out0), .out1(decoder_1_out1), .out2(decoder_1_out2), .out3(decoder_1_out3),
    .out4(decoder_1_out4), .out5(decoder_1_out5), .out6(decoder_1_out6), .out7(decoder_1_out7),
    .out8(decoder_1_out8), .out9(decoder_1_out9), .out10(decoder_1_out10), .out11(decoder_1_out11),
    .out12(decoder_1_out12), .out13(decoder_1_out13), .out14(decoder_1_out14), .out15(decoder_1_out15),
    .sel(column));  // open: en
  or or_1 (or_1_out, reset, _0_if_start_pos_else_1);
  videoadapterRowcontrol videoadapterrowcontrol_1 (
    .id(decoder_1_out0), .rownumb(row), .save(change_value), .reset(or_1_out), .outputValue(out_6));
  videoadapterRowcontrol videoadapterrowcontrol_2 (
    .id(decoder_1_out1), .rownumb(row), .save(change_value), .reset(or_1_out), .outputValue(out_7));
  videoadapterRowcontrol videoadapterrowcontrol_3 (
    .id(decoder_1_out2), .rownumb(row), .save(change_value), .reset(or_1_out), .outputValue(out_8));
  videoadapterRowcontrol videoadapterrowcontrol_4 (
    .id(decoder_1_out3), .rownumb(row), .save(change_value), .reset(or_1_out), .outputValue(out_9));
  videoadapterRowcontrol videoadapterrowcontrol_5 (
    .id(decoder_1_out4), .rownumb(row), .save(change_value), .reset(or_1_out), .outputValue(out_10));
  videoadapterRowcontrol videoadapterrowcontrol_6 (
    .id(decoder_1_out5), .rownumb(row), .save(change_value), .reset(or_1_out), .outputValue(out_11));
  videoadapterRowcontrol videoadapterrowcontrol_7 (
    .id(decoder_1_out6), .rownumb(row), .save(change_value), .reset(or_1_out), .outputValue(out_12));
  videoadapterRowcontrol videoadapterrowcontrol_8 (
    .id(decoder_1_out7), .rownumb(row), .save(change_value), .reset(or_1_out), .outputValue(out_13));
  videoadapterRowcontrol videoadapterrowcontrol_9 (
    .id(decoder_1_out8), .rownumb(row), .save(change_value), .reset(or_1_out), .outputValue(out_14));
  videoadapterRowcontrol videoadapterrowcontrol_10 (
    .id(decoder_1_out9), .rownumb(row), .save(change_value), .reset(or_1_out), .outputValue(out_15));
  videoadapterRowcontrol videoadapterrowcontrol_11 (
    .id(decoder_1_out10), .rownumb(row), .save(change_value), .reset(or_1_out), .outputValue(out_16));
  videoadapterRowcontrol videoadapterrowcontrol_12 (
    .id(decoder_1_out11), .rownumb(row), .save(change_value), .reset(or_1_out), .outputValue(out_17));
  videoadapterRowcontrol videoadapterrowcontrol_13 (
    .id(decoder_1_out12), .rownumb(row), .save(change_value), .reset(or_1_out), .outputValue(out_18));
  videoadapterRowcontrol videoadapterrowcontrol_14 (
    .id(decoder_1_out13), .rownumb(row), .save(change_value), .reset(or_1_out), .outputValue(out_19));
  videoadapterRowcontrol videoadapterrowcontrol_15 (
    .id(decoder_1_out14), .rownumb(row), .save(change_value), .reset(or_1_out), .outputValue(out_20));
  videoadapterRowcontrol videoadapterrowcontrol_16 (
    .id(decoder_1_out15), .rownumb(row), .save(change_value), .reset(or_1_out), .outputValue(out_21));
endmodule

module videoadapterRowcontrol (
  input  id,
  input  [3:0] rownumb,
  input  save,
  input  reset,
  output [15:0] outputValue
);

  wire [15:0] decoder_1_out0, xor_1_out;

  Decoder #(.select(4), .disabled(0)) decoder_1 (
    .out0(decoder_1_out0[0]), .out1(decoder_1_out0[1]), .out2(decoder_1_out0[2]), .out3(decoder_1_out0[3]),
    .out4(decoder_1_out0[4]), .out5(decoder_1_out0[5]), .out6(decoder_1_out0[6]), .out7(decoder_1_out0[7]),
    .out8(decoder_1_out0[8]), .out9(decoder_1_out0[9]), .out10(decoder_1_out0[10]),
    .out11(decoder_1_out0[11]), .out12(decoder_1_out0[12]), .out13(decoder_1_out0[13]),
    .out14(decoder_1_out0[14]), .out15(decoder_1_out0[15]), .sel(rownumb));  // open: en
  Register #(.width(16)) register_1 (.D(xor_1_out), .en(id), .Q(outputValue), .clk(save), .clr(reset));
  assign xor_1_out = decoder_1_out0 ^ outputValue;  // XOR_Gate xor_1, 16 bits wide

  // Notes on the sheet:
  //   reset: pull=down
  //   save: pull=down
  //   rownumb: pull=down
  //   id: pull=down
endmodule

module test (
  input  [3:0] in_1,
  input  [3:0] in_2
);

  wire buffer_1_out, button_1_out, button_2_out, button_3_out, button_4_out, clock_1_out, comparator_1_eq,
       controlled_buffer_1_out, counter_1_q, or_1_out, reader_1_out_20;
  wire [7:0] \reader_1_адрес_говна , \reader_1_значение_говна ;
  wire [15:0] main_1_out_6, main_1_out_7, main_1_out_8, main_1_out_9, main_1_out_10, main_1_out_11,
       main_1_out_12, main_1_out_13, main_1_out_14, main_1_out_15, main_1_out_16, main_1_out_17,
       main_1_out_18, main_1_out_19, main_1_out_20, main_1_out_21;

  Button button_1 (.out(button_1_out));
  or or_1 (or_1_out, comparator_1_eq, button_1_out);
  buf buffer_1 (buffer_1_out, or_1_out);
  Comparator #(.mode("unsigned")) comparator_1 (
    .a({8{1'b1}}), .b(\reader_1_адрес_говна ), .eq(comparator_1_eq));  // open: gt, lt
  Counter #(.width(1), .max('h1)) counter_1 (
    .D(buffer_1_out), .count(buffer_1_out), .Q(counter_1_q), .clk(buffer_1_out));  // open: load, carry, clr
  // Probe on in_2
  // Probe on in_1
  DotMatrix #(.matrixcols(16), .matrixrows(16)) dotmatrix_1 (
    .col0(main_1_out_6), .col1(main_1_out_7), .col2(main_1_out_8), .col3(main_1_out_9), .col4(main_1_out_10),
    .col5(main_1_out_11), .col6(main_1_out_12), .col7(main_1_out_13), .col8(main_1_out_14),
    .col9(main_1_out_15), .col10(main_1_out_16), .col11(main_1_out_17), .col12(main_1_out_18),
    .col13(main_1_out_19), .col14(main_1_out_20), .col15(main_1_out_21));
  main main_1 (
    .column(in_1), .row(in_2), .out_6(main_1_out_6), .out_7(main_1_out_7), .out_8(main_1_out_8),
    .out_9(main_1_out_9), .out_10(main_1_out_10), .out_11(main_1_out_11), .out_12(main_1_out_12),
    .out_13(main_1_out_13), .out_14(main_1_out_14), .out_15(main_1_out_15), .out_16(main_1_out_16),
    .out_17(main_1_out_17), .out_18(main_1_out_18), .out_19(main_1_out_19), .out_20(main_1_out_20),
    .out_21(main_1_out_21), .reset(button_3_out), .change_value(button_4_out));  // open: _0_if_start_pos_else_1
  Clock clock_1 (.out(clock_1_out));
  assign controlled_buffer_1_out = counter_1_q ? clock_1_out : 1'bz;  // Controlled_Buffer controlled_buffer_1
  Button button_2 (.out(button_2_out));
  Button button_3 (.out(button_3_out));
  Button button_4 (.out(button_4_out));
  reader reader_1 (
    .in_1(button_2_out), .in_2(controlled_buffer_1_out), .in_3(main_1_out_6), .in_4(main_1_out_7),
    .in_5(main_1_out_8), .in_6(main_1_out_9), .in_7(main_1_out_10), .in_8(main_1_out_11),
    .in_9(main_1_out_12), .in_10(main_1_out_13), .in_11(main_1_out_14), .in_12(main_1_out_15),
    .in_13(main_1_out_16), .in_14(main_1_out_17), .in_15(main_1_out_18), .in_16(main_1_out_19),
    .in_17(main_1_out_20), .in_18(main_1_out_21), .\адрес_говна (\reader_1_адрес_говна ),
    .\значение_говна (\reader_1_значение_говна ), .out_20(reader_1_out_20));
  \интел_228  \u_интел_228_1  (
    .add(\reader_1_адрес_говна ), .val(\reader_1_значение_говна ), .tact(reader_1_out_20),
    .alusha(comparator_1_eq), .dqbeforeuprbuf(counter_1_q));  // open: in_5
endmodule

module \читатель  (
  input  \сброс ,
  input  \тактовая_залупа ,
  input  [7:0] in_3,
  input  [7:0] in_4,
  input  [15:0] \число_ебать ,
  output [7:0] \адрес_хуйни ,
  output [7:0] \знач 
);

  wire and_1_out, comparator_1_eq, comparator_1_lt, comparator_2_eq, comparator_2_gt, multiplexer_1_out,
       or_1_out, or_2_out;
  wire [3:0] buffer_1_out;
  wire [7:0] bit_extender_1_out;

  // Probe on in_4
  // Probe on in_3
  Multiplexer #(.select(4)) multiplexer_1 (
    .in0(\число_ебать [0]), .in1(\число_ебать [1]), .in2(\число_ебать [2]), .in3(\число_ебать [3]),
    .in4(\число_ебать [4]), .in5(\число_ебать [5]), .in6(\число_ебать [6]), .in7(\число_ебать [7]),
    .in8(\число_ебать [8]), .in9(\число_ебать [9]), .in10(\число_ебать [10]), .in11(\число_ебать [11]),
    .in12(\число_ебать [12]), .in13(\число_ебать [13]), .in14(\число_ебать [14]), .in15(\число_ебать [15]),
    .out(multiplexer_1_out), .sel(buffer_1_out));  // open: en
  // Probe on buffer_1_out
  Comparator #(.mode("unsigned")) comparator_1 (
    .a(in_3), .b(\адрес_хуйни ), .eq(comparator_1_eq), .lt(comparator_1_lt));  // open: gt
  Comparator #(.mode("unsigned")) comparator_2 (
    .a(in_4), .b(\адрес_хуйни ), .gt(comparator_2_gt), .eq(comparator_2_eq));  // open: lt
  assign buffer_1_out = \адрес_хуйни [3:0];  // Buffer buffer_1, 4 bits wide
  assign bit_extender_1_out = {{7{1'b0}}, multiplexer_1_out};  // Bit_Extender bit_extender_1
  or or_1 (or_1_out, comparator_1_lt, comparator_1_eq);
  or or_2 (or_2_out, comparator_2_gt, comparator_2_eq);
  Counter counter_1 (
    .D(\адрес_хуйни ), .count(1'b1), .Q(\адрес_хуйни ), .clk(\тактовая_залупа ), .clr(\сброс ));  // open: load, carry
  and and_1 (and_1_out, or_1_out, or_2_out);
  Pull_Resistor pull_resistor_1 (.node(\знач ));
  Transistor #(.\type ("n"), .width(8)) transistor_1 (.in(bit_extender_1_out), .out(\знач ), .gate(and_1_out));

  // Notes on the sheet:
  //   ot
  //   do
endmodule

module reader (
  input  in_1,
  input  in_2,
  input  [15:0] in_3,
  input  [15:0] in_4,
  input  [15:0] in_5,
  input  [15:0] in_6,
  input  [15:0] in_7,
  input  [15:0] in_8,
  input  [15:0] in_9,
  input  [15:0] in_10,
  input  [15:0] in_11,
  input  [15:0] in_12,
  input  [15:0] in_13,
  input  [15:0] in_14,
  input  [15:0] in_15,
  input  [15:0] in_16,
  input  [15:0] in_17,
  input  [15:0] in_18,
  output [7:0] \адрес_говна ,
  output out_20,
  output [7:0] \значение_говна 
);

  wire comparator_1_eq, transistor_1_out;
  wire [7:0] \читатель_1_адрес_хуйни , \читатель_1_знач , \читатель_2_адрес_хуйни , \читатель_2_знач ,
       \читатель_3_адрес_хуйни , \читатель_3_знач , \читатель_4_адрес_хуйни , \читатель_4_знач ,
       \читатель_5_адрес_хуйни , \читатель_5_знач , \читатель_6_адрес_хуйни , \читатель_6_знач ,
       \читатель_7_адрес_хуйни , \читатель_7_знач , \читатель_8_адрес_хуйни , \читатель_8_знач ,
       \читатель_9_адрес_хуйни , \читатель_9_знач , \читатель_10_адрес_хуйни , \читатель_10_знач ,
       \читатель_11_адрес_хуйни , \читатель_11_знач , \читатель_12_адрес_хуйни , \читатель_12_знач ,
       \читатель_13_адрес_хуйни , \читатель_13_знач , \читатель_14_адрес_хуйни , \читатель_14_знач ,
       \читатель_15_адрес_хуйни , \читатель_15_знач , \читатель_16_адрес_хуйни , \читатель_16_знач ;

  \читатель  \u_читатель_1  (
    .\сброс (in_1), .\тактовая_залупа (transistor_1_out), .\число_ебать (in_3),
    .\адрес_хуйни (\читатель_1_адрес_хуйни ), .\знач (\читатель_1_знач ), .in_4(8'hf), .in_3({8{1'b0}}));
  \читатель  \u_читатель_2  (
    .\сброс (in_1), .\тактовая_залупа (transistor_1_out), .\число_ебать (in_4),
    .\адрес_хуйни (\читатель_2_адрес_хуйни ), .\знач (\читатель_2_знач ), .in_4(8'h1f), .in_3(8'h10));
  \читатель  \u_читатель_3  (
    .\сброс (in_1), .\тактовая_залупа (transistor_1_out), .\число_ебать (in_5),
    .\адрес_хуйни (\читатель_3_адрес_хуйни ), .\знач (\читатель_3_знач ), .in_4(8'h2f), .in_3(8'h20));
  \читатель  \u_читатель_4  (
    .\сброс (in_1), .\тактовая_залупа (transistor_1_out), .\число_ебать (in_6),
    .\адрес_хуйни (\читатель_4_адрес_хуйни ), .\знач (\читатель_4_знач ), .in_4(8'h3f), .in_3(8'h30));
  \читатель  \u_читатель_5  (
    .\сброс (in_1), .\тактовая_залупа (transistor_1_out), .\число_ебать (in_7),
    .\адрес_хуйни (\читатель_5_адрес_хуйни ), .\знач (\читатель_5_знач ), .in_4(8'h4f), .in_3(8'h40));
  \читатель  \u_читатель_6  (
    .\сброс (in_1), .\тактовая_залупа (transistor_1_out), .\число_ебать (in_8),
    .\адрес_хуйни (\читатель_6_адрес_хуйни ), .\знач (\читатель_6_знач ), .in_4(8'h5f), .in_3(8'h50));
  \читатель  \u_читатель_7  (
    .\сброс (in_1), .\тактовая_залупа (transistor_1_out), .\число_ебать (in_9),
    .\адрес_хуйни (\читатель_7_адрес_хуйни ), .\знач (\читатель_7_знач ), .in_4(8'h6f), .in_3(8'h60));
  \читатель  \u_читатель_8  (
    .\сброс (in_1), .\тактовая_залупа (transistor_1_out), .\число_ебать (in_10),
    .\адрес_хуйни (\читатель_8_адрес_хуйни ), .\знач (\читатель_8_знач ), .in_4(8'h7f), .in_3(8'h70));
  \читатель  \u_читатель_9  (
    .\сброс (in_1), .\тактовая_залупа (transistor_1_out), .\число_ебать (in_11),
    .\адрес_хуйни (\читатель_9_адрес_хуйни ), .\знач (\читатель_9_знач ), .in_4(8'h8f), .in_3(8'h80));
  \читатель  \u_читатель_10  (
    .\сброс (in_1), .\тактовая_залупа (transistor_1_out), .\число_ебать (in_12),
    .\адрес_хуйни (\читатель_10_адрес_хуйни ), .\знач (\читатель_10_знач ), .in_4(8'h9f), .in_3(8'h90));
  \читатель  \u_читатель_11  (
    .\сброс (in_1), .\тактовая_залупа (transistor_1_out), .\число_ебать (in_13),
    .\адрес_хуйни (\читатель_11_адрес_хуйни ), .\знач (\читатель_11_знач ), .in_4(8'haf), .in_3(8'ha0));
  \читатель  \u_читатель_12  (
    .\сброс (in_1), .\тактовая_залупа (transistor_1_out), .\число_ебать (in_14),
    .\адрес_хуйни (\читатель_12_адрес_хуйни ), .\знач (\читатель_12_знач ), .in_4(8'hbf), .in_3(8'hb0));
  \читатель  \u_читатель_13  (
    .\сброс (in_1), .\тактовая_залупа (transistor_1_out), .\число_ебать (in_15),
    .\адрес_хуйни (\читатель_13_адрес_хуйни ), .\знач (\читатель_13_знач ), .in_4(8'hcf), .in_3(8'hc0));
  \читатель  \u_читатель_14  (
    .\сброс (in_1), .\тактовая_залупа (transistor_1_out), .\число_ебать (in_16),
    .\адрес_хуйни (\читатель_14_адрес_хуйни ), .\знач (\читатель_14_знач ), .in_4(8'hdf), .in_3(8'hd0));
  \читатель  \u_читатель_15  (
    .\сброс (in_1), .\тактовая_залупа (transistor_1_out), .\число_ебать (in_17),
    .\адрес_хуйни (\читатель_15_адрес_хуйни ), .\знач (\читатель_15_знач ), .in_4(8'hef), .in_3(8'he0));
  \читатель  \u_читатель_16  (
    .\сброс (in_1), .\тактовая_залупа (transistor_1_out), .\число_ебать (in_18),
    .\адрес_хуйни (\читатель_16_адрес_хуйни ), .\знач (\читатель_16_знач ), .in_4({8{1'b1}}), .in_3(8'hf0));
  xor xor_1 (out_20, comparator_1_eq, transistor_1_out);
  Comparator #(.mode("unsigned")) comparator_1 (
    .a({8{1'b1}}), .b(\адрес_говна ), .eq(comparator_1_eq));  // open: gt, lt
  Transistor transistor_1 (.in(in_2), .out(transistor_1_out), .gate(comparator_1_eq));
  Pull_Resistor pull_resistor_1 (.node(transistor_1_out));
  assign \адрес_говна  = \читатель_1_адрес_хуйни  | \читатель_2_адрес_хуйни  | \читатель_3_адрес_хуйни  | \читатель_4_адрес_хуйни  | \читатель_5_адрес_хуйни  | \читатель_6_адрес_хуйни  | \читатель_7_адрес_хуйни  | \читатель_8_адрес_хуйни  | \читатель_9_адрес_хуйни  | \читатель_10_адрес_хуйни  | \читатель_11_адрес_хуйни  | \читатель_12_адрес_хуйни  | \читатель_13_адрес_хуйни  | \читатель_14_адрес_хуйни  | \читатель_15_адрес_хуйни  | \читатель_16_адрес_хуйни ;  // OR_Gate or_1, 8 bits wide
  // Probe on \значение_говна 
  // Probe on \адрес_говна 
  assign \значение_говна  = \читатель_1_знач  | \читатель_2_знач  | \читатель_3_знач  | \читатель_4_знач  | \читатель_5_знач  | \читатель_6_знач  | \читатель_7_знач  | \читатель_8_знач  | \читатель_9_знач  | \читатель_10_знач  | \читатель_11_знач  | \читатель_12_знач  | \читатель_13_знач  | \читатель_14_знач  | \читатель_15_знач  | \читатель_16_знач ;  // OR_Gate or_2, 8 bits wide

  // Notes on the sheet:
  //   значение строк ебаного дисплея\
  //   щелбан чтоб обнулить
  //   щелчок бля для записи
endmodule

module \интел_228  (
  input  [7:0] add,
  input  [7:0] val,
  input  tact,
  input  alusha,
  input  [3:0] in_5,
  input  dqbeforeuprbuf
);

  wire and_1_out, buffer_1_out, button_1_out, button_2_out, cdm_8_mark5_1_p1, cdm_8_mark5_1_p2,
       cdm_8_mark5_1_p4, cdm_8_mark5_1_p5, cdm_8_mark5_1_p7, cdm_8_mark5_1_p8, cdm_8_mark5_1_p9,
       cdm_8_mark5_1_p15, clock_1_out, comparator_1_eq, comparator_2_eq, controlled_buffer_2_out,
       controlled_buffer_6_out, controlled_buffer_9_out, counter_1_q, decoder_1_out0, decoder_1_out1,
       decoder_2_out0, decoder_2_out1, not_1_out, not_2_out, not_3_out, not_4_out, not_5_out, or_1_out,
       or_2_out, or_3_out;
  wire [7:0] cdm_8_mark5_1_p3, cdm_8_mark5_1_p10, cdm_8_mark5_1_p11, cdm_8_mark5_1_p12, cdm_8_mark5_1_p13,
       cdm_8_mark5_1_p14, controlled_buffer_3_out, controlled_buffer_5_out;
  wire [15:0] main_1_out_6, main_1_out_7, main_1_out_8, main_1_out_9, main_1_out_10, main_1_out_11,
       main_1_out_12, main_1_out_13, main_1_out_14, main_1_out_15, main_1_out_16, main_1_out_17,
       main_1_out_18, main_1_out_19, main_1_out_20, main_1_out_21;

  Comparator #(.mode("unsigned")) comparator_1 (.a(cdm_8_mark5_1_p3), .b(8'he4), .eq(comparator_1_eq));  // open: gt, lt
  not not_1 (not_1_out, dqbeforeuprbuf);
  and and_1 (and_1_out, alusha, not_1_out);
  not not_2 (not_2_out, comparator_1_eq);
  buf or_1 (or_1_out, not_2_out);  // OR_Gate
  Clock clock_1 (.out(clock_1_out));
  Button button_1 (.out(button_1_out));
  // Probe on cdm_8_mark5_1_p3
  // Probe on cdm_8_mark5_1_p2
  // Probe on cdm_8_mark5_1_p1
  Controlled_Buffer controlled_buffer_1 (.in(controlled_buffer_2_out), .en(or_1_out));  // open: out
  assign controlled_buffer_2_out = and_1_out ? clock_1_out : 1'bz;  // Controlled_Buffer controlled_buffer_2
  or or_2 (or_2_out, comparator_2_eq, button_1_out);
  buf buffer_1 (buffer_1_out, or_2_out);
  // Probe on cdm_8_mark5_1_p4
  // CdM_8_mark5 cdm_8_mark5_1: pin names not known; wires that end beside it: cdm_8_mark5_1_p1, cdm_8_mark5_1_p2, cdm_8_mark5_1_p3, cdm_8_mark5_1_p4, cdm_8_mark5_1_p5, cdm_8_mark5_1_p5, cdm_8_mark5_1_p7, cdm_8_mark5_1_p8, cdm_8_mark5_1_p9, cdm_8_mark5_1_p10, cdm_8_mark5_1_p11, cdm_8_mark5_1_p12, cdm_8_mark5_1_p13, cdm_8_mark5_1_p14, cdm_8_mark5_1_p15
  assign controlled_buffer_3_out = and_1_out ? cdm_8_mark5_1_p10 : 8'bz;  // Controlled_Buffer controlled_buffer_3
  not not_3 (not_3_out, cdm_8_mark5_1_p9);
  assign cdm_8_mark5_1_p12 = cdm_8_mark5_1_p9 ? controlled_buffer_5_out : 8'bz;  // Controlled_Buffer controlled_buffer_4
  Comparator #(.mode("unsigned")) comparator_2 (
    .a({8{1'b1}}), .b(cdm_8_mark5_1_p13), .eq(comparator_2_eq));  // open: gt, lt
  Counter #(.width(1), .max('h1)) counter_1 (
    .D(buffer_1_out), .count(buffer_1_out), .Q(counter_1_q), .clk(buffer_1_out));  // open: load, carry, clr
  Pull_Resistor pull_resistor_1 (.node(cdm_8_mark5_1_p15));
  Decoder #(.disabled(0)) decoder_1 (
    .out0(decoder_1_out0), .out1(decoder_1_out1), .sel(cdm_8_mark5_1_p7), .en(cdm_8_mark5_1_p8));
  assign controlled_buffer_5_out = not_3_out ? cdm_8_mark5_1_p11 : 8'bz;  // Controlled_Buffer controlled_buffer_5
  // Probe on controlled_buffer_3_out
  Controlled_Buffer controlled_buffer_6 (.out(controlled_buffer_6_out), .en(counter_1_q));  // open: in
  assign cdm_8_mark5_1_p15 = dqbeforeuprbuf ? tact : 1'bz;  // Controlled_Buffer controlled_buffer_7
  main main_1 (
    .column(in_5), .row(in_5), .out_6(main_1_out_6), .out_7(main_1_out_7), .out_8(main_1_out_8),
    .out_9(main_1_out_9), .out_10(main_1_out_10), .out_11(main_1_out_11), .out_12(main_1_out_12),
    .out_13(main_1_out_13), .out_14(main_1_out_14), .out_15(main_1_out_15), .out_16(main_1_out_16),
    .out_17(main_1_out_17), .out_18(main_1_out_18), .out_19(main_1_out_19), .out_20(main_1_out_20),
    .out_21(main_1_out_21), .change_value(button_2_out));  // open: reset, _0_if_start_pos_else_1
  assign controlled_buffer_3_out = dqbeforeuprbuf ? add : 8'bz;  // Controlled_Buffer controlled_buffer_8
  Decoder #(.disabled(0)) decoder_2 (
    .out0(decoder_2_out0), .out1(decoder_2_out1), .sel(cdm_8_mark5_1_p9), .en(decoder_1_out1));
  reader reader_1 (
    .in_2(controlled_buffer_6_out), .in_3(main_1_out_6), .in_4(main_1_out_7), .in_5(main_1_out_8),
    .in_6(main_1_out_9), .in_7(main_1_out_10), .in_8(main_1_out_11), .in_9(main_1_out_12),
    .in_10(main_1_out_13), .in_11(main_1_out_14), .in_12(main_1_out_15), .in_13(main_1_out_16),
    .in_14(main_1_out_17), .in_15(main_1_out_18), .in_16(main_1_out_19), .in_17(main_1_out_20),
    .in_18(main_1_out_21), .\адрес_говна (cdm_8_mark5_1_p13), .\значение_говна (cdm_8_mark5_1_p14));  // open: in_1, out_20
  not not_4 (not_4_out, dqbeforeuprbuf);
  or or_3 (or_3_out, dqbeforeuprbuf, decoder_2_out1);
  not not_5 (not_5_out, cdm_8_mark5_1_p9);
  Button button_2 (.out(button_2_out));
  assign controlled_buffer_9_out = not_4_out ? decoder_1_out0 : 1'bz;  // Controlled_Buffer controlled_buffer_9
  Pull_Resistor pull_resistor_2 (.node(controlled_buffer_9_out));
  Pull_Resistor pull_resistor_3 (.node(decoder_1_out0));
  ROM rom_1 (.addr(controlled_buffer_3_out), .data(controlled_buffer_5_out), .sel(controlled_buffer_9_out));
  RAM #(.bus("separate")) ram_1 (
    .addr(controlled_buffer_3_out), .din(val), .data(controlled_buffer_5_out), .str(cdm_8_mark5_1_p15),
    .sel(or_3_out), .clk(cdm_8_mark5_1_p15), .ld(cdm_8_mark5_1_p9));  // open: clr
  RAM #(.bus("separate")) ram_2 (
    .addr(controlled_buffer_3_out), .din(controlled_buffer_5_out), .str(not_5_out), .sel(decoder_2_out0),
    .clk(clock_1_out));  // open: data, ld, clr

  // Notes on the sheet:
  //   in_5: pull=down
  //   code
  //   поле сейчас (отседа четаем)
  //   поле на след шаге сюда пишем
  //   contents of rom_1 (hex, n*v repeats v):
  //   d1 0 d2 f0 19 b4 13 d2 1 19 b4 13 d2 10 19 b4 13 19 b4 13 89 b4 13 89 b4 13 d2 f0 19 b4 13 19 b4 13
  //   d2 11 19 d2 3 7e e1 2f d2 1 a6 ee 40 b4 0 e0 3d d2 2 7b e1 3b d2 1 a6 ee 40 d2 0 a6 8d d3 0 5 e1 2
  //   d2 f0 19 b4 13 d2 1 19 b4 13 d2 e 19 b4 13 d2 10 19 b4 13 d2 10 19 b4 13 d2 f1 19 b4 13 d2 1 19 b4
  //   13 d2 f0 19 b4 13 89 d2 3 7e e1 79 d2 1 a6 ee 8a b4 0 e0 87 d2 2 7b e1 85 d2 1 a6 ee 8a d2 0 a6 d2
  //   10 19 d3 0 5 e1 46 d1 f d2 f0 19 b4 13 d2 f1 19 b4 13 d2 e 19 b4 13 d2 10 19 b4 13 d2 10 19 b4 13 d2
  //   1 19 b4 13 d2 f1 19 b4 13 d2 f0 19 b4 13 d2 f 19 d2 3 7e e1 c9 d2 1 a6 ee da b4 0 e0 d7 d2 2 7b e1
  //   d5 d2 1 a6 ee da d2 0 a6 d2 10 19 d2 f d3 0 76 e1 94 d2 e4 a e1 0 d4
endmodule
