// Logisim project videoadapterebat2.circ as structural Verilog: 8 circuits, main circuit main
module main (
  input  reset,
  input  change_value,
  input  [3:0] column,
  input  _0_if_start_pos_else_1,
  input  [3:0] row,
  output [15:0] out_6,
  output [15:0] out_7,
  output [15:0] out_8,
  output [15:0] out_9,
  output [15:0] out_10,
  output [15:0] out_11,
  output [15:0] out_12,
  output [15:0] out_13,
  output [15:0] out_14,
  output [15:0] out_15,
  output [15:0] out_16,
  output [15:0] out_17,
  output [15:0] out_18,
  output [15:0] out_19,
  output [15:0] out_20,
  output [15:0] out_21
);

  wire decoder_1_out0, decoder_1_out1, decoder_1_out2, decoder_1_out3, decoder_1_out4, decoder_1_out5,
       decoder_1_out6, decoder_1_out7, decoder_1_out8, decoder_1_out9, decoder_1_out10, decoder_1_out11,
       decoder_1_out12, decoder_1_out13, decoder_1_out14, decoder_1_out15, not_1_out, or_1_out;
  wire [15:0] videoadapterrowcontrol_1_outputvalue, videoadapterrowcontrol_2_outputvalue,
       videoadapterrowcontrol_3_outputvalue, videoadapterrowcontrol_4_outputvalue,
       videoadapterrowcontrol_5_outputvalue, videoadapterrowcontrol_6_outputvalue,
       videoadapterrowcontrol_7_outputvalue, videoadapterrowcontrol_8_outputvalue,
       videoadapterrowcontrol_9_outputvalue, videoadapterrowcontrol_10_outputvalue,
       videoadapterrowcontrol_11_outputvalue, videoadapterrowcontrol_12_outputvalue,
       videoadapterrowcontrol_13_outputvalue, videoadapterrowcontrol_14_outputvalue,
       videoadapterrowcontrol_15_outputvalue, videoadapterrowcontrol_16_outputvalue;

  Decoder #(.select(4)) decoder_1 (
    .out0(decoder_1_out0), .out1(decoder_1_out1), .out2(decoder_1_out2), .out3(decoder_1_out3),
    .out4(decoder_1_out4), .out5(decoder_1_out5), .out6(decoder_1_out6), .out7(decoder_1_out7),
    .out8(decoder_1_out8), .out9(decoder_1_out9), .out10(decoder_1_out10), .out11(decoder_1_out11),
    .out12(decoder_1_out12), .out13(decoder_1_out13), .out14(decoder_1_out14), .out15(decoder_1_out15),
    .sel(column));  // open: en
  buf or_1 (or_1_out, reset);  // OR_Gate
  videoadapterRowcontrol videoadapterrowcontrol_1 (
    .id(decoder_1_out0), .rownumb(row), .save(change_value), .reset(or_1_out),
    .outputValue(videoadapterrowcontrol_1_outputvalue));
  videoadapterRowcontrol videoadapterrowcontrol_2 (
    .id(decoder_1_out1), .rownumb(row), .save(change_value), .reset(or_1_out),
    .outputValue(videoadapterrowcontrol_2_outputvalue));
  videoadapterRowcontrol videoadapterrowcontrol_3 (
    .id(decoder_1_out2), .rownumb(row), .save(change_value), .reset(or_1_out),
    .outputValue(videoadapterrowcontrol_3_outputvalue));
  videoadapterRowcontrol videoadapterrowcontrol_4 (
    .id(decoder_1_out3), .rownumb(row), .save(change_value), .reset(or_1_out),
    .outputValue(videoadapterrowcontrol_4_outputvalue));
  videoadapterRowcontrol videoadapterrowcontrol_5 (
    .id(decoder_1_out4), .rownumb(row), .save(change_value), .reset(or_1_out),
    .outputValue(videoadapterrowcontrol_5_outputvalue));
  videoadapterRowcontrol videoadapterrowcontrol_6 (
    .id(decoder_1_out5), .rownumb(row), .save(change_value), .reset(or_1_out),
    .outputValue(videoadapterrowcontrol_6_outputvalue));
  videoadapterRowcontrol videoadapterrowcontrol_7 (
    .id(decoder_1_out6), .rownumb(row), .save(change_value), .reset(or_1_out),
    .outputValue(videoadapterrowcontrol_7_outputvalue));
  videoadapterRowcontrol videoadapterrowcontrol_8 (
    .id(decoder_1_out7), .rownumb(row), .save(change_value), .reset(or_1_out),
    .outputValue(videoadapterrowcontrol_8_outputvalue));
  videoadapterRowcontrol videoadapterrowcontrol_9 (
    .id(decoder_1_out8), .rownumb(row), .save(change_value), .reset(or_1_out),
    .outputValue(videoadapterrowcontrol_9_outputvalue));
  videoadapterRowcontrol videoadapterrowcontrol_10 (
    .id(decoder_1_out9), .rownumb(row), .save(change_value), .reset(or_1_out),
    .outputValue(videoadapterrowcontrol_10_outputvalue));
  videoadapterRowcontrol videoadapterrowcontrol_11 (
    .id(decoder_1_out10), .rownumb(row), .save(change_value), .reset(or_1_out),
    .outputValue(videoadapterrowcontrol_11_outputvalue));
  videoadapterRowcontrol videoadapterrowcontrol_12 (
    .id(decoder_1_out11), .rownumb(row), .save(change_value), .reset(or_1_out),
    .outputValue(videoadapterrowcontrol_12_outputvalue));
  videoadapterRowcontrol videoadapterrowcontrol_13 (
    .id(decoder_1_out12), .rownumb(row), .save(change_value), .reset(or_1_out),
    .outputValue(videoadapterrowcontrol_13_outputvalue));
  videoadapterRowcontrol videoadapterrowcontrol_14 (
    .id(decoder_1_out13), .rownumb(row), .save(change_value), .reset(or_1_out),
    .outputValue(videoadapterrowcontrol_14_outputvalue));
  videoadapterRowcontrol videoadapterrowcontrol_15 (
    .id(decoder_1_out14), .rownumb(row), .save(change_value), .reset(or_1_out),
    .outputValue(videoadapterrowcontrol_15_outputvalue));
  videoadapterRowcontrol videoadapterrowcontrol_16 (
    .id(decoder_1_out15), .rownumb(row), .save(change_value), .reset(or_1_out),
    .outputValue(videoadapterrowcontrol_16_outputvalue));
  not not_1 (not_1_out, _0_if_start_pos_else_1);
  assign out_6 = not_1_out ? videoadapterrowcontrol_1_outputvalue : 16'bz;  // Controlled_Buffer controlled_buffer_1
  assign out_7 = not_1_out ? videoadapterrowcontrol_2_outputvalue : 16'bz;  // Controlled_Buffer controlled_buffer_2
  assign out_8 = not_1_out ? videoadapterrowcontrol_3_outputvalue : 16'bz;  // Controlled_Buffer controlled_buffer_3
  assign out_9 = not_1_out ? videoadapterrowcontrol_4_outputvalue : 16'bz;  // Controlled_Buffer controlled_buffer_4
  assign out_10 = not_1_out ? videoadapterrowcontrol_5_outputvalue : 16'bz;  // Controlled_Buffer controlled_buffer_5
  assign out_11 = not_1_out ? videoadapterrowcontrol_6_outputvalue : 16'bz;  // Controlled_Buffer controlled_buffer_6
  assign out_12 = not_1_out ? videoadapterrowcontrol_7_outputvalue : 16'bz;  // Controlled_Buffer controlled_buffer_7
  assign out_13 = not_1_out ? videoadapterrowcontrol_8_outputvalue : 16'bz;  // Controlled_Buffer controlled_buffer_8
  assign out_14 = not_1_out ? videoadapterrowcontrol_9_outputvalue : 16'bz;  // Controlled_Buffer controlled_buffer_9
  assign out_15 = not_1_out ? videoadapterrowcontrol_10_outputvalue : 16'bz;  // Controlled_Buffer controlled_buffer_10
  assign out_16 = not_1_out ? videoadapterrowcontrol_11_outputvalue : 16'bz;  // Controlled_Buffer controlled_buffer_11
  assign out_17 = not_1_out ? videoadapterrowcontrol_12_outputvalue : 16'bz;  // Controlled_Buffer controlled_buffer_12
  assign out_18 = not_1_out ? videoadapterrowcontrol_13_outputvalue : 16'bz;  // Controlled_Buffer controlled_buffer_13
  assign out_19 = not_1_out ? videoadapterrowcontrol_14_outputvalue : 16'bz;  // Controlled_Buffer controlled_buffer_14
  assign out_20 = not_1_out ? videoadapterrowcontrol_15_outputvalue : 16'bz;  // Controlled_Buffer controlled_buffer_15
  assign out_21 = not_1_out ? videoadapterrowcontrol_16_outputvalue : 16'bz;  // Controlled_Buffer controlled_buffer_16
endmodule

module videoadapterRowcontrol (
  input  id,
  input  [3:0] rownumb,
  input  save,
  input  reset,
  output [15:0] outputValue
);

  wire [15:0] decoder_1_out0, xor_1_out;

  Decoder #(.select(4), .disabled(0)) decoder_1 (
    .out0(decoder_1_out0[0]), .out1(decoder_1_out0[1]), .out2(decoder_1_out0[2]), .out3(decoder_1_out0[3]),
    .out4(decoder_1_out0[4]), .out5(decoder_1_out0[5]), .out6(decoder_1_out0[6]), .out7(decoder_1_out0[7]),
    .out8(decoder_1_out0[8]), .out9(decoder_1_out0[9]), .out10(decoder_1_out0[10]),
    .out11(decoder_1_out0[11]), .out12(decoder_1_out0[12]), .out13(decoder_1_out0[13]),
    .out14(decoder_1_out0[14]), .out15(decoder_1_out0[15]), .sel(rownumb));  // open: en
  assign xor_1_out = decoder_1_out0 ^ outputValue;  // XOR_Gate xor_1, 16 bits wide
  Register #(.width(16)) register_1 (.D(xor_1_out), .en(id), .Q(outputValue), .clk(save), .clr(reset));

  // Notes on the sheet:
  //   id: pull=down
  //   save: pull=down
  //   reset: pull=down
  //   rownumb: pull=down
endmodule

module test (
  input  [3:0] in_1,
  input  [3:0] in_2
);

  wire buffer_1_out, button_1_out, button_2_out, button_3_out, button_4_out, clock_1_out, comparator_1_eq,
       controlled_buffer_1_out, controlled_buffer_2_out, counter_1_q, counter_2_q, or_1_out,
       pull_resistor_1_node, reader_1_out_20;
  wire [7:0] \reader_1_адрес_говна , \reader_1_значение_говна ;
  wire [15:0] main_1_out_6, main_1_out_7, main_1_out_8, main_1_out_9, main_1_out_10, main_1_out_11,
       main_1_out_12, main_1_out_13, main_1_out_14, main_1_out_15, main_1_out_16, main_1_out_17,
       main_1_out_18, main_1_out_19, main_1_out_20, main_1_out_21;

  Button button_1 (.out(button_1_out));
  Pull_Resistor pull_resistor_1 (.node(pull_resistor_1_node));
  assign controlled_buffer_1_out = 1'b0 ? 1'b1 : 1'bz;  // Controlled_Buffer controlled_buffer_1
  or or_1 (or_1_out, comparator_1_eq, button_1_out);
  buf buffer_1 (buffer_1_out, or_1_out);
  Counter #(.width(1), .max('h1), .ongoal("stay")) counter_1 (
    .count(pull_resistor_1_node), .Q(counter_1_q), .clk(pull_resistor_1_node));  // open: load, D, carry, clr
  Comparator #(.mode("unsigned")) comparator_1 (
    .a({8{1'b1}}), .b(\reader_1_адрес_говна ), .eq(comparator_1_eq));  // open: gt, lt
  LED led_1 (.in(pull_resistor_1_node));
  Counter #(.width(1), .max('h1)) counter_2 (
    .D(buffer_1_out), .count(buffer_1_out), .Q(counter_2_q), .clk(buffer_1_out));  // open: load, carry, clr
  // Probe on in_2
  // Probe on in_1
  LED led_2 (.in(pull_resistor_1_node));
  DotMatrix #(.matrixcols(16), .matrixrows(16)) dotmatrix_1 (
    .col0(main_1_out_6), .col1(main_1_out_7), .col2(main_1_out_8), .col3(main_1_out_9), .col4(main_1_out_10),
    .col5(main_1_out_11), .col6(main_1_out_12), .col7(main_1_out_13), .col8(main_1_out_14),
    .col9(main_1_out_15), .col10(main_1_out_16), .col11(main_1_out_17), .col12(main_1_out_18),
    .col13(main_1_out_19), .col14(main_1_out_20), .col15(main_1_out_21));
  main main_1 (
    .column(in_1), .row(in_2), .out_6(main_1_out_6), .out_7(main_1_out_7), .out_8(main_1_out_8),
    .out_9(main_1_out_9), .out_10(main_1_out_10), .out_11(main_1_out_11), .out_12(main_1_out_12),
    .out_13(main_1_out_13), .out_14(main_1_out_14), .out_15(main_1_out_15), .out_16(main_1_out_16),
    .out_17(main_1_out_17), .out_18(main_1_out_18), .out_19(main_1_out_19), .out_20(main_1_out_20),
    .out_21(main_1_out_21), .reset(button_3_out), .change_value(button_4_out),
    ._0_if_start_pos_else_1(counter_1_q));
  \интел_228  \u_интел_228_1  (
    .in_1(counter_1_q), .add(\reader_1_адрес_говна ), .val(\reader_1_значение_говна ),
    .tact(reader_1_out_20), .dqbeforeuprbuf(counter_2_q), .alusha(comparator_1_eq),
    .out_17(pull_resistor_1_node), .out_7(main_1_out_6), .out_8(main_1_out_7), .out_9(main_1_out_8),
    .out_10(main_1_out_9), .out_11(main_1_out_10), .out_12(main_1_out_11), .out_13(main_1_out_12),
    .out_14(main_1_out_13), .out_15(main_1_out_14), .out_16(main_1_out_15), .out_18(main_1_out_16),
    .out_19(main_1_out_17), .out_20(main_1_out_18), .out_21(main_1_out_19), .out_22(main_1_out_20),
    .out_23(main_1_out_21));
  assign controlled_buffer_2_out = counter_2_q ? clock_1_out : 1'bz;  // Controlled_Buffer controlled_buffer_2
  Button button_2 (.out(button_2_out));
  Button button_3 (.out(button_3_out));
  Button button_4 (.out(button_4_out));
  Clock clock_1 (.out(clock_1_out));
  reader reader_1 (
    .in_1(button_2_out), .in_2(controlled_buffer_2_out), .in_3(main_1_out_6), .in_4(main_1_out_7),
    .in_5(main_1_out_8), .in_6(main_1_out_9), .in_7(main_1_out_10), .in_8(main_1_out_11),
    .in_9(main_1_out_12), .in_10(main_1_out_13), .in_11(main_1_out_14), .in_12(main_1_out_15),
    .in_13(main_1_out_16), .in_14(main_1_out_17), .in_15(main_1_out_18), .in_16(main_1_out_19),
    .in_17(main_1_out_20), .in_18(main_1_out_21), .\адрес_говна (\reader_1_адрес_говна ),
    .\значение_говна (\reader_1_значение_говна ), .out_20(reader_1_out_20));
endmodule

module \читатель  (
  input  \сброс ,
  input  \тактовая_залупа ,
  input  [7:0] in_3,
  input  [7:0] in_4,
  input  [15:0] \число_ебать ,
  output [7:0] \адрес_хуйни ,
  output [7:0] \знач 
);

  wire and_1_out, comparator_1_eq, comparator_1_lt, comparator_2_eq, comparator_2_gt, multiplexer_1_out,
       or_1_out, or_2_out;
  wire [3:0] buffer_1_out;
  wire [7:0] bit_extender_1_out;

  // Probe on in_3
  // Probe on in_4
  Multiplexer #(.select(4)) multiplexer_1 (
    .in0(\число_ебать [0]), .in1(\число_ебать [1]), .in2(\число_ебать [2]), .in3(\число_ебать [3]),
    .in4(\число_ебать [4]), .in5(\число_ебать [5]), .in6(\число_ебать [6]), .in7(\число_ебать [7]),
    .in8(\число_ебать [8]), .in9(\число_ебать [9]), .in10(\число_ебать [10]), .in11(\число_ебать [11]),
    .in12(\число_ебать [12]), .in13(\число_ебать [13]), .in14(\число_ебать [14]), .in15(\число_ебать [15]),
    .out(multiplexer_1_out), .sel(buffer_1_out));  // open: en
  // Probe on buffer_1_out
  Comparator #(.mode("unsigned")) comparator_1 (
    .a(in_3), .b(\адрес_хуйни ), .eq(comparator_1_eq), .lt(comparator_1_lt));  // open: gt
  Comparator #(.mode("unsigned")) comparator_2 (
    .a(in_4), .b(\адрес_хуйни ), .gt(comparator_2_gt), .eq(comparator_2_eq));  // open: lt
  assign buffer_1_out = \адрес_хуйни [3:0];  // Buffer buffer_1, 4 bits wide
  assign bit_extender_1_out = {{7{1'b0}}, multiplexer_1_out};  // Bit_Extender bit_extender_1
  or or_1 (or_1_out, comparator_1_lt, comparator_1_eq);
  or or_2 (or_2_out, comparator_2_gt, comparator_2_eq);
  Counter counter_1 (
    .D(\адрес_хуйни ), .count(1'b1), .Q(\адрес_хуйни ), .clk(\тактовая_залупа ), .clr(\сброс ));  // open: load, carry
  and and_1 (and_1_out, or_1_out, or_2_out);
  Transistor #(.\type ("n"), .width(8)) transistor_1 (.in(bit_extender_1_out), .out(\знач ), .gate(and_1_out));
  Pull_Resistor pull_resistor_1 (.node(\знач ));

  // Notes on the sheet:
  //   ot
  //   do
endmodule

module reader (
  input  in_1,
  input  in_2,
  input  [15:0] in_3,
  input  [15:0] in_4,
  input  [15:0] in_5,
  input  [15:0] in_6,
  input  [15:0] in_7,
  input  [15:0] in_8,
  input  [15:0] in_9,
  input  [15:0] in_10,
  input  [15:0] in_11,
  input  [15:0] in_12,
  input  [15:0] in_13,
  input  [15:0] in_14,
  input  [15:0] in_15,
  input  [15:0] in_16,
  input  [15:0] in_17,
  input  [15:0] in_18,
  output [7:0] \адрес_говна ,
  output out_20,
  output [7:0] \значение_говна 
);

  wire comparator_1_eq, transistor_1_out;
  wire [7:0] \читатель_1_адрес_хуйни , \читатель_1_знач , \читатель_2_адрес_хуйни , \читатель_2_знач ,
       \читатель_3_адрес_хуйни , \читатель_3_знач , \читатель_4_адрес_хуйни , \читатель_4_знач ,
       \читатель_5_адрес_хуйни , \читатель_5_знач , \читатель_6_адрес_хуйни , \читатель_6_знач ,
       \читатель_7_адрес_хуйни , \читатель_7_знач , \читатель_8_адрес_хуйни , \читатель_8_знач ,
       \читатель_9_адрес_хуйни , \читатель_9_знач , \читатель_10_адрес_хуйни , \читатель_10_знач ,
       \читатель_11_адрес_хуйни , \читатель_11_знач , \читатель_12_адрес_хуйни , \читатель_12_знач ,
       \читатель_13_адрес_хуйни , \читатель_13_знач , \читатель_14_адрес_хуйни , \читатель_14_знач ,
       \читатель_15_адрес_хуйни , \читатель_15_знач , \читатель_16_адрес_хуйни , \читатель_16_знач ;

  \читатель  \u_читатель_1  (
    .\сброс (in_1), .\тактовая_залупа (transistor_1_out), .\число_ебать (in_3),
    .\адрес_хуйни (\читатель_1_адрес_хуйни ), .\знач (\читатель_1_знач ), .in_4(8'hf), .in_3({8{1'b0}}));
  \читатель  \u_читатель_2  (
    .\сброс (in_1), .\тактовая_залупа (transistor_1_out), .\число_ебать (in_4),
    .\адрес_хуйни (\читатель_2_адрес_хуйни ), .\знач (\читатель_2_знач ), .in_4(8'h1f), .in_3(8'h10));
  \читатель  \u_читатель_3  (
    .\сброс (in_1), .\тактовая_залупа (transistor_1_out), .\число_ебать (in_5),
    .\адрес_хуйни (\читатель_3_адрес_хуйни ), .\знач (\читатель_3_знач ), .in_4(8'h2f), .in_3(8'h20));
  \читатель  \u_читатель_4  (
    .\сброс (in_1), .\тактовая_залупа (transistor_1_out), .\число_ебать (in_6),
    .\адрес_хуйни (\читатель_4_адрес_хуйни ), .\знач (\читатель_4_знач ), .in_4(8'h3f), .in_3(8'h30));
  \читатель  \u_читатель_5  (
    .\сброс (in_1), .\тактовая_залупа (transistor_1_out), .\число_ебать (in_7),
    .\адрес_хуйни (\читатель_5_адрес_хуйни ), .\знач (\читатель_5_знач ), .in_4(8'h4f), .in_3(8'h40));
  \читатель  \u_читатель_6  (
    .\сброс (in_1), .\тактовая_залупа (transistor_1_out), .\число_ебать (in_8),
    .\адрес_хуйни (\читатель_6_адрес_хуйни ), .\знач (\читатель_6_знач ), .in_4(8'h5f), .in_3(8'h50));
  \читатель  \u_читатель_7  (
    .\сброс (in_1), .\тактовая_залупа (transistor_1_out), .\число_ебать (in_9),
    .\адрес_хуйни (\читатель_7_адрес_хуйни ), .\знач (\читатель_7_знач ), .in_4(8'h6f), .in_3(8'h60));
  \читатель  \u_читатель_8  (
    .\сброс (in_1), .\тактовая_залупа (transistor_1_out), .\число_ебать (in_10),
    .\адрес_хуйни (\читатель_8_адрес_хуйни ), .\знач (\читатель_8_знач ), .in_4(8'h7f), .in_3(8'h70));
  \читатель  \u_читатель_9  (
    .\сброс (in_1), .\тактовая_залупа (transistor_1_out), .\число_ебать (in_11),
    .\адрес_хуйни (\читатель_9_адрес_хуйни ), .\знач (\читатель_9_знач ), .in_4(8'h8f), .in_3(8'h80));
  \читатель  \u_читатель_10  (
    .\сброс (in_1), .\тактовая_залупа (transistor_1_out), .\число_ебать (in_12),
    .\адрес_хуйни (\читатель_10_адрес_хуйни ), .\знач (\читатель_10_знач ), .in_4(8'h9f), .in_3(8'h90));
  \читатель  \u_читатель_11  (
    .\сброс (in_1), .\тактовая_залупа (transistor_1_out), .\число_ебать (in_13),
    .\адрес_хуйни (\читатель_11_адрес_хуйни ), .\знач (\читатель_11_знач ), .in_4(8'haf), .in_3(8'ha0));
  \читатель  \u_читатель_12  (
    .\сброс (in_1), .\тактовая_залупа (transistor_1_out), .\число_ебать (in_14),
    .\адрес_хуйни (\читатель_12_адрес_хуйни ), .\знач (\читатель_12_знач ), .in_4(8'hbf), .in_3(8'hb0));
  \читатель  \u_читатель_13  (
    .\сброс (in_1), .\тактовая_залупа (transistor_1_out), .\число_ебать (in_15),
    .\адрес_хуйни (\читатель_13_адрес_хуйни ), .\знач (\читатель_13_знач ), .in_4(8'hcf), .in_3(8'hc0));
  \читатель  \u_читатель_14  (
    .\сброс (in_1), .\тактовая_залупа (transistor_1_out), .\число_ебать (in_16),
    .\адрес_хуйни (\читатель_14_адрес_хуйни ), .\знач (\читатель_14_знач ), .in_4(8'hdf), .in_3(8'hd0));
  \читатель  \u_читатель_15  (
    .\сброс (in_1), .\тактовая_залупа (transistor_1_out), .\число_ебать (in_17),
    .\адрес_хуйни (\читатель_15_адрес_хуйни ), .\знач (\читатель_15_знач ), .in_4(8'hef), .in_3(8'he0));
  \читатель  \u_читатель_16  (
    .\сброс (in_1), .\тактовая_залупа (transistor_1_out), .\число_ебать (in_18),
    .\адрес_хуйни (\читатель_16_адрес_хуйни ), .\знач (\читатель_16_знач ), .in_4({8{1'b1}}), .in_3(8'hf0));
  xor xor_1 (out_20, comparator_1_eq, transistor_1_out);
  Comparator #(.mode("unsigned")) comparator_1 (
    .a({8{1'b1}}), .b(\адрес_говна ), .eq(comparator_1_eq));  // open: gt, lt
  Transistor transistor_1 (.in(in_2), .out(transistor_1_out), .gate(comparator_1_eq));
  Pull_Resistor pull_resistor_1 (.node(transistor_1_out));
  assign \адрес_говна  = \читатель_1_адрес_хуйни  | \читатель_2_адрес_хуйни  | \читатель_3_адрес_хуйни  | \читатель_4_адрес_хуйни  | \читатель_5_адрес_хуйни  | \читатель_6_адрес_хуйни  | \читатель_7_адрес_хуйни  | \читатель_8_адрес_хуйни  | \читатель_9_адрес_хуйни  | \читатель_10_адрес_хуйни  | \читатель_11_адрес_хуйни  | \читатель_12_адрес_хуйни  | \читатель_13_адрес_хуйни  | \читатель_14_адрес_хуйни  | \читатель_15_адрес_хуйни  | \читатель_16_адрес_хуйни ;  // OR_Gate or_1, 8 bits wide
  // Probe on \значение_говна 
  // Probe on \адрес_говна 
  assign \значение_говна  = \читатель_1_знач  | \читатель_2_знач  | \читатель_3_знач  | \читатель_4_знач  | \читатель_5_знач  | \читатель_6_знач  | \читатель_7_знач  | \читатель_8_знач  | \читатель_9_знач  | \читатель_10_знач  | \читатель_11_знач  | \читатель_12_знач  | \читатель_13_знач  | \читатель_14_знач  | \читатель_15_знач  | \читатель_16_знач ;  // OR_Gate or_2, 8 bits wide

  // Notes on the sheet:
  //   значение строк ебаного дисплея\
  //   щелбан чтоб обнулить
  //   щелчок бля для записи
endmodule

module \интел_228  (
  input  in_1,
  input  [7:0] add,
  input  [7:0] val,
  input  tact,
  input  dqbeforeuprbuf,
  input  alusha,
  output [15:0] out_7,
  output [15:0] out_8,
  output [15:0] out_9,
  output [15:0] out_10,
  output [15:0] out_11,
  output [15:0] out_12,
  output [15:0] out_13,
  output [15:0] out_14,
  output [15:0] out_15,
  output [15:0] out_16,
  output out_17,
  output [15:0] out_18,
  output [15:0] out_19,
  output [15:0] out_20,
  output [15:0] out_21,
  output [15:0] out_22,
  output [15:0] out_23
);

  wire and_1_out, cdm_8_mark5_1_p1, cdm_8_mark5_1_p2, cdm_8_mark5_1_p4, cdm_8_mark5_1_p5, cdm_8_mark5_1_p7,
       cdm_8_mark5_1_p8, cdm_8_mark5_1_p9, clock_1_out, comparator_1_eq, controlled_buffer_2_out,
       controlled_buffer_3_out, controlled_buffer_10_out, decoder_1_out0, decoder_1_out1, decoder_2_out0,
       decoder_2_out1, not_1_out, not_2_out, not_3_out, not_4_out, not_5_out, not_6_out, or_1_out, or_2_out,
       or_4_out, pull_resistor_2_node;
  wire [7:0] aaaaa_1_adres, cdm_8_mark5_1_p3, cdm_8_mark5_1_p10, cdm_8_mark5_1_p11, cdm_8_mark5_1_p12,
       controlled_buffer_4_out, controlled_buffer_6_out, controlled_buffer_9_out, or_3_out,
       pull_resistor_6_node, ram_2_data;
  wire [15:0] aaaaa_1_out_3, aaaaa_1_out_5, aaaaa_1_out_6, aaaaa_1_out_8, aaaaa_1_out_9, aaaaa_1_out_10,
       aaaaa_1_out_11, aaaaa_1_out_12, aaaaa_1_out_13, aaaaa_1_out_14, aaaaa_1_out_15, aaaaa_1_out_16,
       aaaaa_1_out_17, aaaaa_1_out_18, aaaaa_1_out_19, aaaaa_1_out_20;

  Comparator #(.mode("unsigned")) comparator_1 (.a(cdm_8_mark5_1_p3), .b(8'he4), .eq(comparator_1_eq));  // open: gt, lt
  not not_1 (not_1_out, dqbeforeuprbuf);
  and and_1 (and_1_out, alusha, not_1_out);
  not not_2 (not_2_out, comparator_1_eq);
  buf or_1 (or_1_out, not_2_out);  // OR_Gate
  Clock clock_1 (.out(clock_1_out));
  // Probe on cdm_8_mark5_1_p3
  // Probe on cdm_8_mark5_1_p1
  // Probe on cdm_8_mark5_1_p2
  Controlled_Buffer controlled_buffer_1 (.in(controlled_buffer_2_out), .en(or_1_out));  // open: out
  assign controlled_buffer_2_out = and_1_out ? clock_1_out : 1'bz;  // Controlled_Buffer controlled_buffer_2
  assign controlled_buffer_3_out = or_1_out ? clock_1_out : 1'bz;  // Controlled_Buffer controlled_buffer_3
  Pull_Resistor pull_resistor_1 (.node(controlled_buffer_3_out));
  // Probe on cdm_8_mark5_1_p4
  // CdM_8_mark5 cdm_8_mark5_1: pin names not known; wires that end beside it: cdm_8_mark5_1_p1, cdm_8_mark5_1_p2, cdm_8_mark5_1_p3, cdm_8_mark5_1_p4, cdm_8_mark5_1_p5, cdm_8_mark5_1_p5, cdm_8_mark5_1_p7, cdm_8_mark5_1_p8, cdm_8_mark5_1_p9, cdm_8_mark5_1_p10, cdm_8_mark5_1_p11, cdm_8_mark5_1_p12
  assign controlled_buffer_4_out = and_1_out ? cdm_8_mark5_1_p10 : 8'bz;  // Controlled_Buffer controlled_buffer_4
  not not_3 (not_3_out, cdm_8_mark5_1_p9);
  assign cdm_8_mark5_1_p12 = cdm_8_mark5_1_p9 ? controlled_buffer_6_out : 8'bz;  // Controlled_Buffer controlled_buffer_5
  Pull_Resistor pull_resistor_2 (.node(pull_resistor_2_node));
  Decoder #(.disabled(0)) decoder_1 (
    .out0(decoder_1_out0), .out1(decoder_1_out1), .sel(cdm_8_mark5_1_p7), .en(cdm_8_mark5_1_p8));
  assign controlled_buffer_6_out = not_3_out ? cdm_8_mark5_1_p11 : 8'bz;  // Controlled_Buffer controlled_buffer_6
  // Probe on controlled_buffer_4_out
  assign pull_resistor_2_node = dqbeforeuprbuf ? tact : 1'bz;  // Controlled_Buffer controlled_buffer_7
  assign controlled_buffer_4_out = dqbeforeuprbuf ? add : 8'bz;  // Controlled_Buffer controlled_buffer_8
  Decoder #(.disabled(0)) decoder_2 (
    .out0(decoder_2_out0), .out1(decoder_2_out1), .sel(cdm_8_mark5_1_p9), .en(decoder_1_out1));
  assign controlled_buffer_9_out = not_5_out ? controlled_buffer_4_out : 8'bz;  // Controlled_Buffer controlled_buffer_9
  Pull_Resistor pull_resistor_3 (.node(controlled_buffer_9_out));
  not not_4 (not_4_out, dqbeforeuprbuf);
  or or_2 (or_2_out, dqbeforeuprbuf, decoder_2_out1);
  assign or_3_out = pull_resistor_6_node | controlled_buffer_9_out;  // OR_Gate or_3, 8 bits wide
  not not_5 (not_5_out, comparator_1_eq);
  not not_6 (not_6_out, cdm_8_mark5_1_p9);
  assign controlled_buffer_10_out = not_4_out ? decoder_1_out0 : 1'bz;  // Controlled_Buffer controlled_buffer_10
  Pull_Resistor pull_resistor_4 (.node(decoder_1_out0));
  Pull_Resistor pull_resistor_5 (.node(controlled_buffer_10_out));
  or or_4 (or_4_out, decoder_2_out0, comparator_1_eq);
  ROM rom_1 (.addr(controlled_buffer_4_out), .data(controlled_buffer_6_out), .sel(controlled_buffer_10_out));
  RAM #(.bus("separate")) ram_1 (
    .addr(controlled_buffer_4_out), .din(val), .data(controlled_buffer_6_out), .str(pull_resistor_2_node),
    .sel(or_2_out), .clk(pull_resistor_2_node), .ld(cdm_8_mark5_1_p9));  // open: clr
  Pull_Resistor pull_resistor_6 (.node(pull_resistor_6_node));
  RAM #(.bus("separate")) ram_2 (
    .addr(or_3_out), .din(controlled_buffer_6_out), .data(ram_2_data), .str(not_6_out), .sel(or_4_out),
    .clk(controlled_buffer_3_out), .ld(comparator_1_eq));  // open: clr
  assign pull_resistor_6_node = comparator_1_eq ? aaaaa_1_adres : 8'bz;  // Controlled_Buffer controlled_buffer_11
  AAAAA aaaaa_1 (
    .vihod(ram_2_data), .adres(aaaaa_1_adres), .\сигнал_что_эта_штука_должна_работать (comparator_1_eq),
    .out_7(out_17), .out_3(aaaaa_1_out_3), .out_5(aaaaa_1_out_5), .out_6(aaaaa_1_out_6),
    .out_8(aaaaa_1_out_8), .out_9(aaaaa_1_out_9), .out_10(aaaaa_1_out_10), .out_11(aaaaa_1_out_11),
    .out_12(aaaaa_1_out_12), .out_13(aaaaa_1_out_13), .out_14(aaaaa_1_out_14), .out_15(aaaaa_1_out_15),
    .out_16(aaaaa_1_out_16), .out_17(aaaaa_1_out_17), .out_18(aaaaa_1_out_18), .out_19(aaaaa_1_out_19),
    .out_20(aaaaa_1_out_20));
  assign out_23 = in_1 ? aaaaa_1_out_20 : 16'bz;  // Controlled_Buffer controlled_buffer_12
  assign out_7 = in_1 ? aaaaa_1_out_3 : 16'bz;  // Controlled_Buffer controlled_buffer_13
  assign out_8 = in_1 ? aaaaa_1_out_5 : 16'bz;  // Controlled_Buffer controlled_buffer_14
  assign out_9 = in_1 ? aaaaa_1_out_6 : 16'bz;  // Controlled_Buffer controlled_buffer_15
  assign out_10 = in_1 ? aaaaa_1_out_8 : 16'bz;  // Controlled_Buffer controlled_buffer_16
  assign out_11 = in_1 ? aaaaa_1_out_9 : 16'bz;  // Controlled_Buffer controlled_buffer_17
  assign out_12 = in_1 ? aaaaa_1_out_10 : 16'bz;  // Controlled_Buffer controlled_buffer_18
  assign out_13 = in_1 ? aaaaa_1_out_11 : 16'bz;  // Controlled_Buffer controlled_buffer_19
  assign out_14 = in_1 ? aaaaa_1_out_12 : 16'bz;  // Controlled_Buffer controlled_buffer_20
  assign out_15 = in_1 ? aaaaa_1_out_13 : 16'bz;  // Controlled_Buffer controlled_buffer_21
  assign out_16 = in_1 ? aaaaa_1_out_14 : 16'bz;  // Controlled_Buffer controlled_buffer_22
  assign out_18 = in_1 ? aaaaa_1_out_15 : 16'bz;  // Controlled_Buffer controlled_buffer_23
  assign out_19 = in_1 ? aaaaa_1_out_16 : 16'bz;  // Controlled_Buffer controlled_buffer_24
  assign out_20 = in_1 ? aaaaa_1_out_17 : 16'bz;  // Controlled_Buffer controlled_buffer_25
  assign out_21 = in_1 ? aaaaa_1_out_18 : 16'bz;  // Controlled_Buffer controlled_buffer_26
  assign out_22 = in_1 ? aaaaa_1_out_19 : 16'bz;  // Controlled_Buffer controlled_buffer_27

  // Notes on the sheet:
  //   code
  //   поле сейчас (отседа четаем)
  //   поле на след шаге сюда пишем
  //   contents of rom_1 (hex, n*v repeats v):
  //   d1 0 d2 f0 19 b4 13 d2 1 19 b4 13 d2 10 19 b4 13 19 b4 13 89 b4 13 89 b4 13 d2 f0 19 b4 13 19 b4 13
  //   d2 11 19 d2 3 7e e1 2f d2 1 a6 ee 40 b4 0 e0 3d d2 2 7b e1 3b d2 1 a6 ee 40 d2 0 a6 8d d3 0 5 e1 2
  //   d2 f0 19 b4 13 d2 1 19 b4 13 d2 e 19 b4 13 d2 10 19 b4 13 d2 10 19 b4 13 d2 f1 19 b4 13 d2 1 19 b4
  //   13 d2 f0 19 b4 13 89 d2 3 7e e1 79 d2 1 a6 ee 8a b4 0 e0 87 d2 2 7b e1 85 d2 1 a6 ee 8a d2 0 a6 d2
  //   10 19 d3 0 5 e1 46 d1 f d2 f0 19 b4 13 d2 f1 19 b4 13 d2 e 19 b4 13 d2 10 19 b4 13 d2 10 19 b4 13 d2
  //   1 19 b4 13 d2 f1 19 b4 13 d2 f0 19 b4 13 d2 f 19 d2 3 7e e1 c9 d2 1 a6 ee da b4 0 e0 d7 d2 2 7b e1
  //   d5 d2 1 a6 ee da d2 0 a6 d2 10 19 d2 f d3 0 76 e1 94 d2 e4 a e1 0 d4
endmodule

module AAAAA (
  input  [7:0] vihod,
  input  \сигнал_что_эта_штука_должна_работать ,
  output [15:0] out_3,
  output [7:0] adres,
  output [15:0] out_5,
  output [15:0] out_6,
  output out_7,
  output [15:0] out_8,
  output [15:0] out_9,
  output [15:0] out_10,
  output [15:0] out_11,
  output [15:0] out_12,
  output [15:0] out_13,
  output [15:0] out_14,
  output [15:0] out_15,
  output [15:0] out_16,
  output [15:0] out_17,
  output [15:0] out_18,
  output [15:0] out_19,
  output [15:0] out_20
);

  wire clock_1_out, comparator_1_eq, controlled_buffer_2_out, controlled_buffer_3_out, decoder_1_out0,
       decoder_1_out1, decoder_1_out2, decoder_1_out3, decoder_1_out4, decoder_1_out5, decoder_1_out6,
       decoder_1_out7, decoder_1_out8, decoder_1_out9, decoder_1_out10, decoder_1_out11, decoder_1_out12,
       decoder_1_out13, decoder_1_out14, decoder_1_out15, not_1_out, not_2_out;
  wire [1:0] counter_1_q;
  wire [7:0] counter_2_q;

  Clock clock_1 (.out(clock_1_out));
  Counter #(.width(2), .max('h3)) counter_1 (
    .count(comparator_1_eq), .Q(counter_1_q), .clk(comparator_1_eq), .clr(not_1_out));  // open: load, D, carry
  not not_1 (not_1_out, \сигнал_что_эта_штука_должна_работать );
  not not_2 (not_2_out, out_7);
  assign adres = \сигнал_что_эта_штука_должна_работать  ? counter_2_q : 8'bz;  // Controlled_Buffer controlled_buffer_1
  assign controlled_buffer_2_out = \сигнал_что_эта_штука_должна_работать  ? clock_1_out : 1'bz;  // Controlled_Buffer controlled_buffer_2
  Counter counter_2 (
    .count(controlled_buffer_3_out), .Q(counter_2_q), .clk(controlled_buffer_3_out), .clr(out_7));  // open: load, D, carry
  assign controlled_buffer_3_out = not_2_out ? controlled_buffer_2_out : 1'bz;  // Controlled_Buffer controlled_buffer_3
  Comparator #(.mode("unsigned")) comparator_1 (.a({8{1'b0}}), .b(counter_2_q), .eq(comparator_1_eq));  // open: gt, lt
  Comparator #(.width(2), .mode("unsigned")) comparator_2 (.a(counter_1_q), .b(2'b01), .eq(out_7));  // open: gt, lt
  Decoder #(.select(4), .disabled(0)) decoder_1 (
    .out0(decoder_1_out0), .out1(decoder_1_out1), .out2(decoder_1_out2), .out3(decoder_1_out3),
    .out4(decoder_1_out4), .out5(decoder_1_out5), .out6(decoder_1_out6), .out7(decoder_1_out7),
    .out8(decoder_1_out8), .out9(decoder_1_out9), .out10(decoder_1_out10), .out11(decoder_1_out11),
    .out12(decoder_1_out12), .out13(decoder_1_out13), .out14(decoder_1_out14), .out15(decoder_1_out15),
    .sel(adres[7:4]));  // open: en
  \ФФФФФФФФ  \u_фффффффф_1  (
    ._4_high_bits(adres[7:4]), .VAL(vihod), ._4_low_bits(adres[3:0]), .dcdr(decoder_1_out0),
    .pulse(controlled_buffer_3_out), .\КОЛЁСА_ДОЛЖНЫ_ВРАЩАТЬСЯ (\сигнал_что_эта_штука_должна_работать ),
    .out_8(out_3), .\константа (4'b0000));
  \ФФФФФФФФ  \u_фффффффф_2  (
    ._4_high_bits(adres[7:4]), .VAL(vihod), ._4_low_bits(adres[3:0]), .dcdr(decoder_1_out1),
    .pulse(controlled_buffer_3_out), .\КОЛЁСА_ДОЛЖНЫ_ВРАЩАТЬСЯ (\сигнал_что_эта_штука_должна_работать ),
    .out_8(out_5), .\константа (4'b0001));
  \ФФФФФФФФ  \u_фффффффф_3  (
    ._4_high_bits(adres[7:4]), .VAL(vihod), ._4_low_bits(adres[3:0]), .dcdr(decoder_1_out2),
    .pulse(controlled_buffer_3_out), .\КОЛЁСА_ДОЛЖНЫ_ВРАЩАТЬСЯ (\сигнал_что_эта_штука_должна_работать ),
    .out_8(out_6), .\константа (4'b0010));
  \ФФФФФФФФ  \u_фффффффф_4  (
    ._4_high_bits(adres[7:4]), .VAL(vihod), ._4_low_bits(adres[3:0]), .dcdr(decoder_1_out3),
    .pulse(controlled_buffer_3_out), .\КОЛЁСА_ДОЛЖНЫ_ВРАЩАТЬСЯ (\сигнал_что_эта_штука_должна_работать ),
    .out_8(out_8), .\константа (4'b0011));
  \ФФФФФФФФ  \u_фффффффф_5  (
    ._4_high_bits(adres[7:4]), .VAL(vihod), ._4_low_bits(adres[3:0]), .dcdr(decoder_1_out4),
    .pulse(controlled_buffer_3_out), .\КОЛЁСА_ДОЛЖНЫ_ВРАЩАТЬСЯ (\сигнал_что_эта_штука_должна_работать ),
    .out_8(out_9), .\константа (4'b0100));
  \ФФФФФФФФ  \u_фффффффф_6  (
    ._4_high_bits(adres[7:4]), .VAL(vihod), ._4_low_bits(adres[3:0]), .dcdr(decoder_1_out5),
    .pulse(controlled_buffer_3_out), .\КОЛЁСА_ДОЛЖНЫ_ВРАЩАТЬСЯ (\сигнал_что_эта_штука_должна_работать ),
    .out_8(out_10), .\константа (4'b0101));
  \ФФФФФФФФ  \u_фффффффф_7  (
    ._4_high_bits(adres[7:4]), .VAL(vihod), ._4_low_bits(adres[3:0]), .dcdr(decoder_1_out6),
    .pulse(controlled_buffer_3_out), .\КОЛЁСА_ДОЛЖНЫ_ВРАЩАТЬСЯ (\сигнал_что_эта_штука_должна_работать ),
    .out_8(out_11), .\константа (4'b0110));
  \ФФФФФФФФ  \u_фффффффф_8  (
    ._4_high_bits(adres[7:4]), .VAL(vihod), ._4_low_bits(adres[3:0]), .dcdr(decoder_1_out7),
    .pulse(controlled_buffer_3_out), .\КОЛЁСА_ДОЛЖНЫ_ВРАЩАТЬСЯ (\сигнал_что_эта_штука_должна_работать ),
    .out_8(out_12), .\константа (4'b0111));
  \ФФФФФФФФ  \u_фффффффф_9  (
    ._4_high_bits(adres[7:4]), .VAL(vihod), ._4_low_bits(adres[3:0]), .dcdr(decoder_1_out8),
    .pulse(controlled_buffer_3_out), .\КОЛЁСА_ДОЛЖНЫ_ВРАЩАТЬСЯ (\сигнал_что_эта_штука_должна_работать ),
    .out_8(out_13), .\константа (4'b1000));
  \ФФФФФФФФ  \u_фффффффф_10  (
    ._4_high_bits(adres[7:4]), .VAL(vihod), ._4_low_bits(adres[3:0]), .dcdr(decoder_1_out9),
    .pulse(controlled_buffer_3_out), .\КОЛЁСА_ДОЛЖНЫ_ВРАЩАТЬСЯ (\сигнал_что_эта_штука_должна_работать ),
    .out_8(out_14), .\константа (4'b1001));
  \ФФФФФФФФ  \u_фффффффф_11  (
    ._4_high_bits(adres[7:4]), .VAL(vihod), ._4_low_bits(adres[3:0]), .dcdr(decoder_1_out10),
    .pulse(controlled_buffer_3_out), .\КОЛЁСА_ДОЛЖНЫ_ВРАЩАТЬСЯ (\сигнал_что_эта_штука_должна_работать ),
    .out_8(out_15), .\константа (4'b1010));
  \ФФФФФФФФ  \u_фффффффф_12  (
    ._4_high_bits(adres[7:4]), .VAL(vihod), ._4_low_bits(adres[3:0]), .dcdr(decoder_1_out11),
    .pulse(controlled_buffer_3_out), .\КОЛЁСА_ДОЛЖНЫ_ВРАЩАТЬСЯ (\сигнал_что_эта_штука_должна_работать ),
    .out_8(out_16), .\константа (4'b1011));
  \ФФФФФФФФ  \u_фффффффф_13  (
    ._4_high_bits(adres[7:4]), .VAL(vihod), ._4_low_bits(adres[3:0]), .dcdr(decoder_1_out12),
    .pulse(controlled_buffer_3_out), .\КОЛЁСА_ДОЛЖНЫ_ВРАЩАТЬСЯ (\сигнал_что_эта_штука_должна_работать ),
    .out_8(out_17), .\константа (4'b1100));
  \ФФФФФФФФ  \u_фффффффф_14  (
    ._4_high_bits(adres[7:4]), .VAL(vihod), ._4_low_bits(adres[3:0]), .dcdr(decoder_1_out13),
    .pulse(controlled_buffer_3_out), .\КОЛЁСА_ДОЛЖНЫ_ВРАЩАТЬСЯ (\сигнал_что_эта_штука_должна_работать ),
    .out_8(out_18), .\константа (4'b1101));
  \ФФФФФФФФ  \u_фффффффф_15  (
    ._4_high_bits(adres[7:4]), .VAL(vihod), ._4_low_bits(adres[3:0]), .dcdr(decoder_1_out14),
    .pulse(controlled_buffer_3_out), .\КОЛЁСА_ДОЛЖНЫ_ВРАЩАТЬСЯ (\сигнал_что_эта_штука_должна_работать ),
    .out_8(out_19), .\константа (4'b1110));
  \ФФФФФФФФ  \u_фффффффф_16  (
    ._4_high_bits(adres[7:4]), .VAL(vihod), ._4_low_bits(adres[3:0]), .dcdr(decoder_1_out15),
    .pulse(controlled_buffer_3_out), .\КОЛЁСА_ДОЛЖНЫ_ВРАЩАТЬСЯ (\сигнал_что_эта_штука_должна_работать ),
    .out_8(out_20), .\константа (4'b1111));
endmodule

module \ФФФФФФФФ  (
  input  [3:0] _4_high_bits,
  input  [3:0] \константа ,
  input  [7:0] VAL,
  input  [3:0] _4_low_bits,
  input  dcdr,
  input  pulse,
  input  \КОЛЁСА_ДОЛЖНЫ_ВРАЩАТЬСЯ ,
  output [15:0] out_8
);

  wire comparator_1_eq, controlled_buffer_1_out, counter_1_q, nor_1_out, not_1_out;
  wire [7:0] demultiplexer_1_out0, demultiplexer_1_out1, demultiplexer_1_out2, demultiplexer_1_out3,
       demultiplexer_1_out4, demultiplexer_1_out5, demultiplexer_1_out6, demultiplexer_1_out7,
       demultiplexer_1_out8, demultiplexer_1_out9, demultiplexer_1_out10, demultiplexer_1_out11,
       demultiplexer_1_out12, demultiplexer_1_out13, demultiplexer_1_out14, demultiplexer_1_out15;
  wire [15:0] or_1_out;

  Comparator #(.width(4), .mode("unsigned")) comparator_1 (
    .a(_4_high_bits), .b(\константа ), .eq(comparator_1_eq));  // open: gt, lt
  Demultiplexer #(.select(4), .width(8), .tristate("true")) demultiplexer_1 (
    .out0(demultiplexer_1_out0), .out1(demultiplexer_1_out1), .out2(demultiplexer_1_out2),
    .out3(demultiplexer_1_out3), .out4(demultiplexer_1_out4), .out5(demultiplexer_1_out5),
    .out6(demultiplexer_1_out6), .out7(demultiplexer_1_out7), .out8(demultiplexer_1_out8),
    .out9(demultiplexer_1_out9), .out10(demultiplexer_1_out10), .out11(demultiplexer_1_out11),
    .out12(demultiplexer_1_out12), .out13(demultiplexer_1_out13), .out14(demultiplexer_1_out14),
    .out15(demultiplexer_1_out15), .in(VAL), .sel(_4_low_bits));  // open: en
  Pull_Resistor pull_resistor_1 (.node({demultiplexer_1_out15[0], demultiplexer_1_out14[0], demultiplexer_1_out13[0], demultiplexer_1_out12[0], demultiplexer_1_out11[0], demultiplexer_1_out10[0], demultiplexer_1_out9[0], demultiplexer_1_out8[0], demultiplexer_1_out7[0], demultiplexer_1_out6[0], demultiplexer_1_out5[0], demultiplexer_1_out4[0], demultiplexer_1_out3[0], demultiplexer_1_out2[0], demultiplexer_1_out1[0], demultiplexer_1_out0[0]}));
  assign or_1_out = {demultiplexer_1_out15[0], demultiplexer_1_out14[0], demultiplexer_1_out13[0], demultiplexer_1_out12[0], demultiplexer_1_out11[0], demultiplexer_1_out10[0], demultiplexer_1_out9[0], demultiplexer_1_out8[0], demultiplexer_1_out7[0], demultiplexer_1_out6[0], demultiplexer_1_out5[0], demultiplexer_1_out4[0], demultiplexer_1_out3[0], demultiplexer_1_out2[0], demultiplexer_1_out1[0], demultiplexer_1_out0[0]} | out_8;  // OR_Gate or_1, 16 bits wide
  Register #(.width(16)) register_1 (.D(or_1_out), .en(dcdr), .Q(out_8), .clk(pulse), .clr(controlled_buffer_1_out));
  assign controlled_buffer_1_out = not_1_out ? comparator_1_eq : 1'bz;  // Controlled_Buffer controlled_buffer_1
  Pull_Resistor pull_resistor_2 (.node(controlled_buffer_1_out));
  not not_1 (not_1_out, counter_1_q);
  Pull_Resistor pull_resistor_3 (.node(comparator_1_eq));
  Counter #(.width(1), .max('h1)) counter_1 (
    .count(controlled_buffer_1_out), .Q(counter_1_q), .clk(controlled_buffer_1_out), .clr(nor_1_out));  // open: load, D, carry
  nor nor_1 (nor_1_out, comparator_1_eq, \КОЛЁСА_ДОЛЖНЫ_ВРАЩАТЬСЯ );
endmodule
